# Fritzing sketch Projeto AVA - João Roberto Bond da Silva ADS117 (saved by Fritzing 0.9.3b)
circuit board: 8.46667cm x 5.64444cm
breadboards: 1

parts:
  Componente1 = Arduino Uno (Rev3)
  LED-VERMELHO = LED - 5mm [color="Red (633nm)" package="5 mm [THT]"]
  LED-AZUL = LED - 5mm [color="Blue (525nm)" package="5 mm [THT]"]
  DS1 = DS18B20 1-Wire Temperature Sensor [part_number=DS18B20]
  RAZUL = Resistor [tolerance=±5% resistance=100 package=THT]
  RVERMELHO = Resistor [tolerance=±5% resistance=100 package=THT]
  RSENSOR = Resistor [tolerance=±5% resistance=4.7 package=THT]
  RDHT = Resistor [tolerance=±5% resistance=4.7 package=THT]
  DHT1 = DHT11 Humitidy and Temperature Sensor

nets (from the pcb view):
  N1: Componente1.A5/SCL, RDHT.Pin_1, DHT1.DATA
  N2: Componente1.D8, DS1.DQ, RSENSOR.Pin_1
  GND: Componente1.GND, RDHT.Pin_0, DHT1.GND
  N3: Componente1.D2, RVERMELHO.Pin_1
  N4: Componente1.D3_PWM, RAZUL.Pin_1
  N5: LED-VERMELHO.cathode, LED-AZUL.cathode
  N6: LED-VERMELHO.anode, RVERMELHO.Pin_0
  N7: LED-AZUL.anode, RAZUL.Pin_0
  N8: DS1.VDD, RSENSOR.Pin_0

custom parts:
  DHT11 Humitidy and Temperature Sensor: DHT11 Humidity and Temperature Sensor
